# Fritzing sketch schedule (saved by Fritzing 1.0.1rc)
breadboards: 1

parts:
  Part1 = Arduino Uno (Rev3)
  R1 = Resistor [tolerance=±5% power=0.25 resistance=10k package=THT]
  R2 = Resistor [tolerance=±5% power=0.25 resistance=1k package=THT]
  S1 = Pushbutton [package=THT]
  R3 = Resistor [tolerance=±5% power=0.25 resistance=1k package=THT]

nets:
  N1: Part1.D8, R1.Pin_0, S1.leg0
  N2: Part1.D0/RX, R2.Pin_0
  N3: Part1.D1/TX, R3.Pin_0
  N4: Part1.5V, S1.leg1
  N5: Part1.GND, R1.Pin_1

notes:
  DV-SV8F board pin GND
  DV-SV8F board pin TX
  DV-SV8F board pin RX
  DV-SV8F board pin 5V
